# Fritzing sketch 模組主控_v1 (saved by Fritzing 0.9.10b)
perfboards: 2

parts:
  DS2Y-5-DC5V2 = DS2Y-5-DC5V [part_number=DS2Y-5-DC5V]  # not connected
  U3 = 74HC595 [package="DIP16 [THT]"]  # not connected
  U4 = PCF8574 [package="DIP16 [THT]"]  # not connected
  IC3 = IC, DIP package, 8 pins [chip_label=LM393]
  IC4 = IC, DIP package, 8 pins [chip_label=L9110H]  # not connected
  J11 = female pin header, 3 pins [form="♀ (female)"]  # not connected
  J12 = female pin header, 3 pins [form="♀ (female)"]  # not connected
  J13 = male pin header, 8 pins [form="♂ (male)"]  # not connected
  J14 = female pin header, 4 pins [form="♀ (female)"]  # not connected
  R15 = Resistor [tolerance=±5% power=0.25 resistance=220 package=THT]  # not connected
  R16 = Resistor [tolerance=±5% power=0.25 resistance=220 package=THT]  # not connected
  R17 = Resistor [tolerance=±5% power=0.25 resistance=220 package=THT]  # not connected
  SW3 = DIP SWITCH [package=dipswitch-02]
  SW4 = DIP SWITCH [package=dipswitch-02]
  R18 = Resistor [tolerance=±5% power=0.25 resistance=220 package=THT]  # not connected
  R19 = Resistor [tolerance=±5% power=0.25 resistance=220 package=THT]  # not connected
  J15 = male pin header, 3 pins [form="♂ (male)"]  # not connected
  R20 = Resistor [tolerance=±5% power=0.25 resistance=220 package=THT]  # not connected
  R21 = Resistor [tolerance=±5% power=0.25 resistance=220 package=THT]
  Q3 = NPN-Transistor [package="TO92 [THT]"]  # not connected
  Q4 = NPN-Transistor [package="TO92 [THT]"]  # not connected
  J16 = male pin header, 3 pins [form="♂ (male)"]  # not connected
  J17 = female pin header, 2 pins [form="♀ (female)"]  # not connected
  J18 = male pin header, 2 pins [form="♂ (male)"]  # not connected
  J19 = male pin header, 2 pins [form="♂ (male)"]  # not connected
  R22 = Resistor [tolerance=±5% power=0.25 resistance=220 package=THT]  # not connected
  R23 = Trimmer Potentiometer [maximum_resistance=10kΩ knob_status=50% power=0.25W package=THT]  # not connected
  R24 = Trimmer Potentiometer [maximum_resistance=10kΩ knob_status=50% power=0.25W package=THT]  # not connected
  J20 = male pin header, 4 pins [form="♂ (male)"]  # not connected
  R25 = Resistor [tolerance=±5% power=0.25 resistance=220 package=THT]
  LED3 = LED - 5mm [color="Red (633nm)" current=0.030 package="5 mm [THT]"]
  LED4 = LED - 5mm [color="Green (565nm)" current=0.030 package="5 mm [THT]"]  # not connected
  R26 = Resistor [tolerance=±5% power=0.25 resistance=220 package=THT]  # not connected
  J21 = male pin header, 4 pins [form="♂ (male)"]  # not connected
  J22 = male pin header, 4 pins [form="♂ (male)"]  # not connected
  J23 = male pin header, 4 pins [form="♂ (male)"]  # not connected
  Power_plug1 = Power plug
  J24 = male pin header, 2 pins [form="♂ (male)"]
  Power_plug2 = Power plug
  U5 = RJ45 Jack [package=rj45-8]  # not connected
  U6 = RJ45 Jack [package=rj45-8]  # not connected
  J25 = female pin header, 8 pins [form="♀ (female)"]  # not connected
  J26 = female pin header, 8 pins [form="♀ (female)"]  # not connected
  S1 = Pushbutton [package="[THT]"]
  R27 = Resistor [tolerance=±5% power=0.25 resistance=220 package=THT]  # not connected
  R28 = Resistor [tolerance=±5% power=0.25 resistance=220 package=THT]  # not connected
  LED5 = LED - 5mm [color="Red (633nm)" current=0.030 package="5 mm [THT]"]  # not connected
  J28 = male pin header, 4 pins [form="♂ (male)"]  # not connected
  J27 = male pin header, 3 pins [form="♂ (male)"]  # not connected
  J29 = Screw terminal - 2 pins [package=THT]  # not connected
  J30 = male pin header, 2 pins [form="♂ (male)"]  # not connected
  LED6 = LED - 5mm [color="Red (633nm)" current=0.030 package="5 mm [THT]"]  # not connected
  R29 = Resistor [tolerance=±5% power=0.25 resistance=220 package=THT]  # not connected
  J31 = Screw terminal - 2 pins [package=THT]  # not connected

nets:
  N1: IC3.pin8, R21.Pin_0
  N2: SW3.2, SW4.1
  N3: SW3.3, SW4.4
  N4: R25.Pin_0, LED3.anode
  GND: Power_plug1.GND, J24.pin2, Power_plug2.GND
  VCC: Power_plug1.VCC, J24.pin1, Power_plug2.VCC
  N5: S1.Pin_1, S1.Pin_2
  N6: S1.Pin_3, S1.Pin_4
